// Logisim project ProjectMain (1).circ as structural Verilog: 3 circuits, main circuit main
module main (
  input  in_1,
  output [2:0] out_2,
  output [2:0] out_3,
  output [2:0] out_4,
  output Cout,
  output [4:0] out_6,
  output Overflow
);

  wire AluSrc, and_1_out, Beq, Bne, BSlt1, BSlt2, Cin, CLK, Flag, LoadEnb, MemEnable, n7_segment_1_a,
       n7_segment_1_b, n7_segment_1_c, n7_segment_1_d, n7_segment_1_e, n7_segment_1_f, n7_segment_1_g,
       n7_segment_2_a, n7_segment_2_b, n7_segment_2_c, n7_segment_2_d, n7_segment_2_e, n7_segment_2_f,
       n7_segment_2_g, n7_segment_3_a, n7_segment_3_b, n7_segment_3_c, n7_segment_3_d, n7_segment_3_e,
       n7_segment_3_f, n7_segment_3_g, n7_segment_4_a, n7_segment_4_b, n7_segment_4_c, n7_segment_4_d,
       n7_segment_4_e, n7_segment_4_f, n7_segment_4_g, PC, RegDes, RegSrc, RegWrite, StoreEnb, xor_1_out,
       ZERO;
  wire [1:1] multiplexer_2_out;
  wire [2:0] multiplexer_3_out;
  wire [3:0] _0_3, _4_7, _8_11, _12_15;
  wire [4:0] JopcodeComp, OpCode;
  wire [7:0] adder_1_out, adder_2_out, adder_3_out, bit_extender_7_out, bit_extender_10_out,
       multiplexer_1_out, register_1_q;
  wire [8:0] Jaddress;
  wire [13:0] bit_extender_9_out, DATA, main_1_output_b, multiplexer_4_out, multiplexer_5_out,
       n14bitalu_1_result, ram_1_data, Store;
  wire [15:0] rom_1_data;

  Clock clock_1 (.out(CLK));
  Register register_1 (.D(multiplexer_1_out), .Q(register_1_q), .clk(CLK), .clr(in_1));  // open: en
  MainControlUnit maincontrolunit_1 (
    .Flag(Flag), .Op4(out_6[4]), .DSlt(RegDes), .Op3(out_6[3]), .Op2(out_6[2]), .Op1(out_6[1]),
    .Op0(out_6[0]), .SrcSlt(RegSrc), .RW(RegWrite), .L(LoadEnb), .S(StoreEnb), .Mem(MemEnable),
    .AluSrc(AluSrc), .Beq(Beq), .Bne(Bne), .BSlt1(BSlt1), .BSlt2(BSlt2), .PC(PC));
  Adder adder_1 (.a(8'h1), .b(register_1_q), .out(adder_1_out));  // open: cin, cout
  assign Jaddress = {{1{1'b0}}, rom_1_data[7:0]};  // Bit_Extender bit_extender_1
  Bit_Extender #(.out_width(5)) bit_extender_2 (.in(rom_1_data[15:8]), .out(JopcodeComp));
  ROM #(.dataWidth(16)) rom_1 (.addr(register_1_q), .data(rom_1_data));  // open: sel
  Multiplexer #(.select(2), .width(8), .enable("false")) multiplexer_1 (
    .in0(adder_1_out), .in1(adder_1_out), .in2(adder_2_out), .in3(adder_3_out), .out(multiplexer_1_out),
    .sel({multiplexer_2_out[1], PC}));
  Multiplexer #(.select(2), .enable("false")) multiplexer_2 (
    .in0(and_1_out), .in1(xor_1_out), .in2(Flag), .in3(1'b0), .out(multiplexer_2_out[1]), .sel({BSlt1, BSlt2}));
  Bit_Extender #(.in_width(4), .out_width(3)) bit_extender_3 (.in(rom_1_data[3:0]), .out(out_2));
  Bit_Extender #(.in_width(4), .out_width(3)) bit_extender_4 (.in(rom_1_data[7:4]), .out(out_3));
  Bit_Extender #(.in_width(4), .out_width(3)) bit_extender_5 (.in(rom_1_data[11:8]), .out(out_4));
  assign out_6 = {{1{1'b0}}, rom_1_data[15:12]};  // Bit_Extender bit_extender_6
  assign bit_extender_7_out = {{5{1'b0}}, out_2};  // Bit_Extender bit_extender_7
  and and_1 (and_1_out, Beq, ZERO);
  ALUcontrol alucontrol_1 (
    .O4(out_6[4]), .O3(out_6[3]), .O2(out_6[2]), .O1(out_6[1]), .O0(out_6[0]), .S4(OpCode[4]),
    .S3(OpCode[3]), .S2(OpCode[2]), .S1(OpCode[1]), .S0(OpCode[0]), .Cin(Cin));
  xor xor_1 (xor_1_out, ZERO, Bne);
  Adder adder_2 (.a(adder_1_out), .b(bit_extender_7_out), .out(adder_2_out));  // open: cin, cout
  Multiplexer #(.width(3), .enable("false")) multiplexer_3 (
    .in0(out_2), .in1(out_4), .out(multiplexer_3_out), .sel(RegDes));
  assign {_12_15, _8_11, _4_7, _0_3} = {{2{1'b0}}, DATA};  // Bit_Extender bit_extender_8
  Register_File__14_bit__main main_1 (
    .Data_in(DATA), .regWrite(RegWrite), .Output_A(Store), .Output_B(main_1_output_b),
    .Data_Address(multiplexer_3_out), .Address_A(out_4), .Address_B(out_3), .in_6(CLK));
  Comparator #(.width(5)) comparator_1 (.a(5'b10000), .b(JopcodeComp), .eq(Flag));  // open: gt, lt
  Multiplexer #(.width(14), .enable("false")) multiplexer_4 (
    .in0(Store), .in1(main_1_output_b), .out(multiplexer_4_out), .sel(RegSrc));
  Multiplexer #(.width(14), .enable("false")) multiplexer_5 (
    .in0(main_1_output_b), .in1(bit_extender_9_out), .out(multiplexer_5_out), .sel(RegSrc));
  assign bit_extender_9_out = {{11{1'b0}}, out_2};  // Bit_Extender bit_extender_9
  Bit_Extender #(.in_width(9), .out_width(8)) bit_extender_10 (.in(Jaddress), .out(bit_extender_10_out));
  Adder adder_3 (.a(bit_extender_10_out), .b(adder_1_out), .out(adder_3_out));  // open: cin, cout
  _14bitALU u_14bitalu_1 (
    .in_1(Cin), .A(multiplexer_4_out), .LESS(1'b0), .B(multiplexer_5_out), .RESULT(n14bitalu_1_result),
    .ZERO(ZERO), .Cout(Cout), .OVERFLOW(Overflow), .OpCode(OpCode));
  _7_segment u_7_segment_1 (
    .d3(_0_3[3]), .d2(_0_3[2]), .d1(_0_3[1]), .d0(_0_3[0]), .a(n7_segment_1_a), .b(n7_segment_1_b),
    .c(n7_segment_1_c), .d(n7_segment_1_d), .e(n7_segment_1_e), .f(n7_segment_1_f), .g(n7_segment_1_g));
  _7_segment u_7_segment_2 (
    .d3(_4_7[3]), .d2(_4_7[2]), .d1(_4_7[1]), .d0(_4_7[0]), .a(n7_segment_2_a), .b(n7_segment_2_b),
    .c(n7_segment_2_c), .d(n7_segment_2_d), .e(n7_segment_2_e), .f(n7_segment_2_f), .g(n7_segment_2_g));
  _7_segment u_7_segment_3 (
    .d3(_8_11[3]), .d2(_8_11[2]), .d1(_8_11[1]), .d0(_8_11[0]), .a(n7_segment_3_a), .b(n7_segment_3_b),
    .c(n7_segment_3_c), .d(n7_segment_3_d), .e(n7_segment_3_e), .f(n7_segment_3_f), .g(n7_segment_3_g));
  _7_segment u_7_segment_4 (
    .d3(_12_15[3]), .d2(_12_15[2]), .d1(_12_15[1]), .d0(_12_15[0]), .a(n7_segment_4_a), .b(n7_segment_4_b),
    .c(n7_segment_4_c), .d(n7_segment_4_d), .e(n7_segment_4_e), .f(n7_segment_4_f), .g(n7_segment_4_g));
  _7_Segment_Display u_7_segment_display_1 (
    .g(n7_segment_1_g), .f(n7_segment_1_f), .a(n7_segment_1_a), .b(n7_segment_1_b), .e(n7_segment_1_e),
    .d(n7_segment_1_d), .c(n7_segment_1_c));  // open: dp
  RAM #(.addrWidth(14), .dataWidth(14), .bus("separate")) ram_1 (
    .addr(n14bitalu_1_result), .din(Store), .data(ram_1_data), .str(StoreEnb), .sel(MemEnable), .clk(CLK),
    .ld(LoadEnb));  // open: clr
  _7_Segment_Display u_7_segment_display_2 (
    .g(n7_segment_2_g), .f(n7_segment_2_f), .a(n7_segment_2_a), .b(n7_segment_2_b), .e(n7_segment_2_e),
    .d(n7_segment_2_d), .c(n7_segment_2_c));  // open: dp
  _7_Segment_Display u_7_segment_display_3 (
    .g(n7_segment_3_g), .f(n7_segment_3_f), .a(n7_segment_3_a), .b(n7_segment_3_b), .e(n7_segment_3_e),
    .d(n7_segment_3_d), .c(n7_segment_3_c));  // open: dp
  _7_Segment_Display u_7_segment_display_4 (
    .g(n7_segment_4_g), .f(n7_segment_4_f), .a(n7_segment_4_a), .b(n7_segment_4_b), .e(n7_segment_4_e),
    .d(n7_segment_4_d), .c(n7_segment_4_c));  // open: dp
  Multiplexer #(.width(14), .enable("false")) multiplexer_6 (
    .in0(n14bitalu_1_result), .in1(ram_1_data), .out(DATA), .sel(AluSrc));

  // Other names for the same wires on the sheet: OP[4:0] = out_6; Op0 = out_6[0]; Op1 = out_6[1]; Op2 = out_6[2];
  //   Op3 = out_6[3]; Op4 = out_6[4]; Rd[2:0] = out_2; Rs[2:0] = out_4; Rt[2:0] = out_3

  // Notes on the sheet:
  //   contents of rom_1 (hex, n*v repeats v):
  //   1120 675 a122 2462 d712 705 1215 8152 9206 10f8
endmodule

// Main Control
module MainControlUnit (
  input  Flag,
  input  Op4,
  input  Op3,
  input  Op2,
  input  Op1,
  input  Op0,
  output DSlt,
  output SrcSlt,
  output RW,
  output L,
  output S,
  output Mem,
  output AluSrc,
  output Beq,
  output Bne,
  output BSlt1,
  output BSlt2,
  output PC
);

  wire and_1_out, and_2_out, and_3_out, and_4_out, and_5_out, and_6_out, and_7_out, and_8_out, and_9_out,
       and_14_out, and_15_out, and_16_out, and_17_out, and_18_out, not_1_out, not_2_out, not_3_out,
       not_4_out, not_5_out, not_6_out, not_7_out, not_8_out, not_9_out, not_10_out, not_11_out, not_12_out,
       not_13_out, not_14_out, not_15_out, not_16_out, not_17_out, not_18_out, not_19_out, not_20_out,
       not_22_out, not_23_out, not_24_out;

  not not_1 (not_1_out, Op3);
  not not_2 (not_2_out, Op0);
  not not_3 (not_3_out, Op2);
  not not_4 (not_4_out, Op1);
  not not_5 (not_5_out, Op3);
  not not_6 (not_6_out, Op0);
  not not_7 (not_7_out, Op1);
  not not_8 (not_8_out, Flag);
  not not_9 (not_9_out, Op3);
  not not_10 (not_10_out, Flag);
  not not_11 (not_11_out, Op1);
  not not_12 (not_12_out, Op0);
  not not_13 (not_13_out, Op0);
  not not_14 (not_14_out, Op2);
  not not_15 (not_15_out, Op1);
  not not_16 (not_16_out, Op2);
  not not_17 (not_17_out, Op1);
  not not_18 (not_18_out, Op2);
  not not_19 (not_19_out, Op0);
  not not_20 (not_20_out, Op2);
  not not_21 (BSlt1, Op3);
  not not_22 (not_22_out, Flag);
  not not_23 (not_23_out, Op3);
  not not_24 (not_24_out, Op2);
  and and_1 (and_1_out, not_1_out, Op1, not_2_out);
  and and_2 (and_2_out, Op2, Op1, Op0);
  and and_3 (and_3_out, Op3, not_3_out);
  and and_4 (and_4_out, Op3, not_4_out);
  and and_5 (and_5_out, not_5_out, Op1, not_6_out);
  and and_6 (and_6_out, Op2, Op1, Op0);
  and and_7 (and_7_out, Op3, not_7_out);
  and and_8 (and_8_out, not_8_out, not_9_out);
  and and_9 (and_9_out, not_10_out, not_11_out, not_12_out);
  or or_1 (L, not_13_out, Op1);
  and and_10 (Mem, Op3, not_14_out, not_15_out);
  and and_11 (AluSrc, Op3, not_16_out, not_17_out);
  and and_12 (Beq, Op3, not_18_out, Op1, not_19_out);
  and and_13 (Bne, Op3, not_20_out, Op1, Op0);
  and and_14 (and_14_out, not_22_out, not_23_out, Op0);
  and and_15 (and_15_out, Op1, Op0);
  and and_16 (and_16_out, Op3, not_24_out, Op0);
  and and_17 (and_17_out, Op4, Op0);
  and and_18 (and_18_out, Flag, Op2, Op0);
  or or_2 (DSlt, and_1_out, and_2_out, and_3_out, and_4_out);
  or or_3 (SrcSlt, and_5_out, and_6_out, and_7_out);
  or or_4 (RW, and_8_out, and_9_out, Op2);
  or or_5 (BSlt2, and_14_out, and_15_out, and_16_out, and_17_out, and_18_out);

  assign PC = Flag;
  assign S = Op0;
endmodule

// ALU Control
module ALUcontrol (
  input  O4,
  input  O3,
  input  O2,
  input  O1,
  input  O0,
  output S4,
  output S3,
  output S2,
  output S1,
  output S0,
  output Cin
);

  wire and_3_out, and_4_out, and_5_out, and_6_out, and_7_out, and_8_out, and_9_out, and_10_out, and_11_out,
       and_12_out, and_13_out, not_1_out, not_2_out, not_3_out, not_4_out, not_5_out, not_6_out, not_7_out,
       not_8_out, not_9_out, not_10_out, not_11_out, not_12_out, not_13_out, not_14_out, not_15_out,
       not_16_out, not_17_out;

  not not_1 (not_1_out, O1);
  not not_2 (not_2_out, O1);
  not not_3 (not_3_out, O0);
  not not_4 (not_4_out, O1);
  not not_5 (not_5_out, O4);
  not not_6 (not_6_out, O0);
  not not_7 (not_7_out, O3);
  not not_8 (not_8_out, O3);
  not not_9 (not_9_out, O0);
  not not_10 (not_10_out, O3);
  not not_11 (not_11_out, O2);
  not not_12 (not_12_out, O1);
  not not_13 (not_13_out, O1);
  not not_14 (not_14_out, O0);
  not not_15 (not_15_out, O3);
  not not_16 (not_16_out, O2);
  not not_17 (not_17_out, O1);
  and and_1 (S4, O3, O2, not_1_out, O0);
  and and_2 (S3, O3, O2, not_2_out, not_3_out);
  and and_3 (and_3_out, O2, not_4_out, O0);
  and and_4 (and_4_out, not_5_out, O3, O2);
  and and_5 (and_5_out, O3, O2, not_6_out);
  and and_6 (and_6_out, not_7_out, O1, O0);
  and and_7 (and_7_out, not_8_out, O2, not_9_out);
  and and_8 (and_8_out, not_10_out, not_11_out, not_12_out, O0);
  and and_9 (and_9_out, O2, not_13_out, not_14_out);
  and and_10 (and_10_out, O2, O1, O0);
  and and_11 (and_11_out, O3, O1);
  and and_12 (and_12_out, not_15_out, not_16_out, not_17_out, O0);
  and and_13 (and_13_out, O3, O1);
  or or_1 (S2, and_3_out, and_4_out, and_5_out);
  or or_2 (S1, and_6_out, and_7_out);
  or or_3 (S0, and_8_out, and_9_out, and_10_out, and_11_out);
  or or_4 (Cin, and_12_out, and_13_out);
endmodule
