// Logisim project ROMloaded.circ as structural Verilog: 1 circuit, main circuit main
module main (
  input  [7:0] in_1,
  output [15:0] out_2,
  output [2:0] out_3,
  output [2:0] out_4,
  output [2:0] out_5,
  output [4:0] out_6,
  output [2:0] out_7,
  output [2:0] out_8,
  output [2:0] out_9,
  output [4:0] out_10
);

  ROM #(.dataWidth(16)) rom_1 (.addr(in_1), .data(out_2));  // open: sel
  Bit_Extender #(.in_width(4), .out_width(3)) bit_extender_1 (.in(out_2[3:0]), .out(out_3));
  Bit_Extender #(.in_width(4), .out_width(3)) bit_extender_2 (.in(out_2[7:4]), .out(out_4));
  Bit_Extender #(.in_width(4), .out_width(3)) bit_extender_3 (.in(out_2[11:8]), .out(out_5));
  assign out_6 = {{1{1'b0}}, out_2[15:12]};  // Bit_Extender bit_extender_4
  Bit_Extender #(.in_width(4), .out_width(3)) bit_extender_5 (.out(out_7));  // open: in
  Bit_Extender #(.in_width(4), .out_width(3)) bit_extender_6 (.out(out_8));  // open: in
  Bit_Extender #(.in_width(3), .out_width(5)) bit_extender_7 (.out(out_10));  // open: in

  // Notes on the sheet:
  //   contents of rom_1 (hex, n*v repeats v):
  //   201 1730 a122 8453
endmodule
