// Logisim project Register File (14 bit).circ as structural Verilog: 2 circuits, main circuit main
// 14 bit register
module main (
  input  [13:0] Data_in,
  input  regWrite,
  input  [2:0] Address_A,
  input  [2:0] Data_Address,
  input  [2:0] Address_B,
  input  in_6,
  output [13:0] Output_A,
  output [13:0] Output_B
);

  wire and_1_out, and_2_out, and_3_out, and_4_out, and_5_out, and_6_out, and_7_out, and_8_out,
       decoder_1_out0, decoder_1_out1, decoder_1_out2, decoder_1_out3, decoder_1_out4, decoder_1_out5,
       decoder_1_out6, decoder_1_out7;
  wire [13:0] T0_q, T1_q, T2_q, T3_q, T4_q, T5_q, T6_q, T7_q;

  Decoder #(.select(3), .enable("false")) decoder_1 (
    .out0(decoder_1_out0), .out1(decoder_1_out1), .out2(decoder_1_out2), .out3(decoder_1_out3),
    .out4(decoder_1_out4), .out5(decoder_1_out5), .out6(decoder_1_out6), .out7(decoder_1_out7),
    .sel(Data_Address));
  and and_1 (and_1_out, regWrite, decoder_1_out0);
  and and_2 (and_2_out, regWrite, decoder_1_out1);
  and and_3 (and_3_out, regWrite, decoder_1_out2);
  and and_4 (and_4_out, regWrite, decoder_1_out3);
  Register #(.width(14)) T0 (.D(Data_in), .en(and_1_out), .Q(T0_q), .clk(in_6));  // open: clr
  Register #(.width(14)) T1 (.D(Data_in), .en(and_2_out), .Q(T1_q), .clk(in_6));  // open: clr
  Register #(.width(14)) T2 (.D(Data_in), .en(and_3_out), .Q(T2_q), .clk(in_6));  // open: clr
  Register #(.width(14)) T3 (.D(Data_in), .en(and_4_out), .Q(T3_q), .clk(in_6));  // open: clr
  and and_5 (and_5_out, regWrite, decoder_1_out4);
  and and_6 (and_6_out, regWrite, decoder_1_out5);
  and and_7 (and_7_out, regWrite, decoder_1_out6);
  and and_8 (and_8_out, regWrite, decoder_1_out7);
  Register #(.width(14)) T4 (.D(Data_in), .en(and_5_out), .Q(T4_q), .clk(in_6));  // open: clr
  Register #(.width(14)) T5 (.D(Data_in), .en(and_6_out), .Q(T5_q), .clk(in_6));  // open: clr
  Register #(.width(14)) T6 (.D(Data_in), .en(and_7_out), .Q(T6_q), .clk(in_6));  // open: clr
  Register #(.width(14)) T7 (.D(Data_in), .en(and_8_out), .Q(T7_q), .clk(in_6));  // open: clr
  Multiplexer #(.select(3), .width(14), .enable("false")) multiplexer_1 (
    .in0(T0_q), .in1(T1_q), .in2(T2_q), .in3(T3_q), .in4(T4_q), .in5(T5_q), .in6(T6_q), .in7(T7_q),
    .out(Output_A), .sel(Address_A));
  Multiplexer #(.select(3), .width(14), .enable("false")) multiplexer_2 (
    .in0(T0_q), .in1(T1_q), .in2(T2_q), .in3(T3_q), .in4(T4_q), .in5(T5_q), .in6(T6_q), .in7(T7_q),
    .out(Output_B), .sel(Address_B));
endmodule

module Register_File_Block_Diagram (
  input  [13:0] in_1,
  input  WE,
  input  [2:0] WR,
  input  [2:0] RR1,
  input  [2:0] RR2,
  input  CLK,
  output [13:0] out_7,
  output [13:0] out_8
);

  main main_1 (
    .Data_in(in_1), .regWrite(WE), .Output_A(out_7), .Output_B(out_8), .Data_Address(WR), .Address_A(RR1),
    .Address_B(RR2), .in_6(CLK));

  // Notes on the sheet:
  //   DATA IN
  //   RD1
  //   RD2
endmodule
