// Logisim project projectALU.circ as structural Verilog: 2 circuits, main circuit main
module main (
  input  Cin,
  input  A,
  input  B,
  input  LESS,
  input  [4:0] OPCODE,
  output RESULT,
  output Negative,
  output Cout
);

  wire and_1_out, multiplexer_1_out, not_1_out, not_2_out, or_1_out, or_2_out;

  not not_1 (not_1_out, B);
  Multiplexer #(.enable("false")) multiplexer_1 (.in0(B), .in1(not_1_out), .out(multiplexer_1_out), .sel(or_2_out));
  Adder #(.width(1)) adder_1 (.a(A), .b(multiplexer_1_out), .out(Negative), .cin(Cin), .cout(Cout));
  and and_1 (and_1_out, A, B);
  or or_1 (or_1_out, A, B);
  not not_2 (not_2_out, or_1_out);
  Multiplexer #(.select(5), .enable("false")) multiplexer_2 (
    .in0(Negative), .in1(Negative), .in2(and_1_out), .in3(or_1_out), .in4(not_2_out), .in5(LESS),
    .out(RESULT), .sel(OPCODE));  // open: in6, in7, in8, in9, in10, in11, in12, in13, in14, in15, in16, in17, in18, in19, in20, in21, in22, in23, in24, in25, in26, in27, in28, in29, in30, in31
  or or_2 (or_2_out, OPCODE[1], OPCODE[0]);

  // Notes on the sheet:
  //   000 - ADD
  //   001 - SUB
  //   010 - AND
  //   011 - OR
  //   100 - NOR
  //   101 - LESS
endmodule

module _14bitALU (
  input  in_1,
  input  [13:0] A,
  input  LESS,
  input  [13:0] B,
  input  [4:0] OpCode,
  output [13:0] RESULT,
  output ZERO,
  output Cout,
  output OVERFLOW
);

  wire main_1_cout, main_2_cout, main_3_cout, main_4_cout, main_5_cout, main_6_cout, main_7_cout,
       main_8_cout, main_9_cout, main_10_cout, main_11_cout, main_12_cout, main_13_cout, N0, N1, N2, N3, N4,
       N5, N6, N7, N8, N9, N10, N11, N12, N13, or_1_out, R0, R1, R2, R3, R4, R5, R6, R7, R8, R9, R10, R11,
       R12, R13;
  wire [3:0] bit_extender_1_out;
  wire [4:0] bit_extender_2_out;
  wire [13:0] SLL, SRL;

  Bit_Extender #(.in_width(14), .out_width(4)) bit_extender_1 (.in(B), .out(bit_extender_1_out));
  Shifter #(.width(14)) shifter_1 (.in(A), .\dist (bit_extender_1_out), .out(SLL));
  Shifter #(.width(14), .shift("lr")) shifter_2 (.in(A), .\dist (bit_extender_1_out), .out(SRL));
  assign bit_extender_2_out = {{2{1'b0}}, OpCode[2:0]};  // Bit_Extender bit_extender_2
  main main_1 (
    .A(A[0]), .B(B[0]), .LESS(N13), .RESULT(R0), .OPCODE(bit_extender_2_out), .Negative(N0),
    .Cout(main_1_cout), .Cin(in_1));
  main main_2 (
    .A(A[1]), .B(B[1]), .LESS(LESS), .RESULT(R1), .OPCODE(bit_extender_2_out), .Negative(N1),
    .Cout(main_2_cout), .Cin(main_1_cout));
  main main_3 (
    .A(A[2]), .B(B[2]), .LESS(LESS), .RESULT(R2), .OPCODE(bit_extender_2_out), .Negative(N2),
    .Cout(main_3_cout), .Cin(main_2_cout));
  main main_4 (
    .A(A[3]), .B(B[3]), .LESS(LESS), .RESULT(R3), .OPCODE(bit_extender_2_out), .Negative(N3),
    .Cout(main_4_cout), .Cin(main_3_cout));
  main main_5 (
    .A(A[4]), .B(B[4]), .LESS(LESS), .RESULT(R4), .OPCODE(bit_extender_2_out), .Negative(N4),
    .Cout(main_5_cout), .Cin(main_4_cout));
  main main_6 (
    .A(A[5]), .B(B[5]), .LESS(LESS), .RESULT(R5), .OPCODE(bit_extender_2_out), .Negative(N5),
    .Cout(main_6_cout), .Cin(main_5_cout));
  main main_7 (
    .A(A[6]), .B(B[6]), .LESS(LESS), .RESULT(R6), .OPCODE(bit_extender_2_out), .Negative(N6),
    .Cout(main_7_cout), .Cin(main_6_cout));
  main main_8 (
    .A(A[7]), .B(B[7]), .LESS(LESS), .RESULT(R7), .OPCODE(bit_extender_2_out), .Negative(N7),
    .Cout(main_8_cout), .Cin(main_7_cout));
  main main_9 (
    .A(A[8]), .B(B[8]), .LESS(LESS), .RESULT(R8), .OPCODE(bit_extender_2_out), .Negative(N8),
    .Cout(main_9_cout), .Cin(main_8_cout));
  main main_10 (
    .A(A[9]), .B(B[9]), .LESS(LESS), .RESULT(R9), .OPCODE(bit_extender_2_out), .Negative(N9),
    .Cout(main_10_cout), .Cin(main_9_cout));
  main main_11 (
    .A(A[10]), .B(B[10]), .LESS(LESS), .RESULT(R10), .OPCODE(bit_extender_2_out), .Negative(N10),
    .Cout(main_11_cout), .Cin(main_10_cout));
  main main_12 (
    .A(A[11]), .B(B[11]), .LESS(LESS), .RESULT(R11), .OPCODE(bit_extender_2_out), .Negative(N11),
    .Cout(main_12_cout), .Cin(main_11_cout));
  main main_13 (
    .A(A[12]), .B(B[12]), .LESS(LESS), .RESULT(R12), .OPCODE(bit_extender_2_out), .Negative(N12),
    .Cout(main_13_cout), .Cin(main_12_cout));
  main main_14 (
    .A(A[13]), .B(B[13]), .LESS(LESS), .RESULT(R13), .OPCODE(bit_extender_2_out), .Negative(N13),
    .Cout(Cout), .Cin(main_13_cout));
  or or_1 (or_1_out, R0, R1, R2, R3, R4, R5, R6, R7, R8, R9, R10, R11, R12, R13);
  xor xor_1 (OVERFLOW, main_13_cout, Cout);
  Multiplexer #(.select(2), .width(14), .enable("false")) multiplexer_1 (
    .in0({R13, R12, R11, R10, R9, R8, R7, R6, R5, R4, R3, R2, R1, R0}), .in1(SLL), .in2(SRL), .out(RESULT),
    .sel(OpCode[4:3]));  // open: in3
  not not_1 (ZERO, or_1_out);

  // Other names for the same wires on the sheet: RES_SLL_SRL[1:0] = OpCode[4:3]
endmodule
